// Logisim project mcdxxxiini.circ as structural Verilog
module ALU (
  input  cf,
  input  ic,
  input  op3,
  input  op2,
  input  op1,
  input  op0,
  input  [31:0] X,
  input  [31:0] Y,
  output [3:0] flags,
  output [31:0] Xout,
  output [31:0] Yout
);

  wire [3:0] arithmetic_unit_1_flags, logical_unit_1_flags;
  wire [31:0] arithmetic_unit_1_xout, arithmetic_unit_1_yout, logical_unit_1_xout, logical_unit_1_yout;

  logical_unit logical_unit_1 (
    .ic(ic), .cf(cf), .op2(op2), .op1(op1), .op0(op0), .X(X), .Y(Y), .flags(logical_unit_1_flags),
    .Xout(logical_unit_1_xout), .Yout(logical_unit_1_yout));
  arithmetic_unit arithmetic_unit_1 (
    .ic(ic), .op2(op2), .op1(op1), .op0(op0), .X(X), .Y(Y), .flags(arithmetic_unit_1_flags),
    .Xout(arithmetic_unit_1_xout), .Yout(arithmetic_unit_1_yout));
  Multiplexer #(.width(32)) multiplexer_1 (
    .in0(logical_unit_1_xout), .in1(arithmetic_unit_1_xout), .out(Xout), .sel(op3));
  Multiplexer #(.width(32)) multiplexer_2 (
    .in0(logical_unit_1_yout), .in1(arithmetic_unit_1_yout), .out(Yout), .sel(op3));
  Multiplexer #(.width(4)) multiplexer_3 (
    .in0(logical_unit_1_flags), .in1(arithmetic_unit_1_flags), .out(flags), .sel(op3));
endmodule

module arithmetic_unit (
  input  ic,
  input  op2,
  input  op1,
  input  op0,
  input  [31:0] X,
  input  [31:0] Y,
  output [3:0] flags,
  output [31:0] Xout,
  output [31:0] Yout
);

  wire adder_1_cout;
  wire [4:0] bit_extender_1_out;
  wire [31:0] adder_1_out, divider_1_out, divider_1_rem, multiplier_1_cout, multiplier_1_out, negator_1_out,
       shifter_1_out, shifter_2_out, subtractor_1_out, undriven;

  Adder #(.width(32)) adder_1 (.a(X), .b(Y), .out(adder_1_out), .cout(adder_1_cout));  // open: cin
  Subtractor #(.width(32)) subtractor_1 (.a(X), .b(Y), .out(subtractor_1_out));  // open: bin, bout
  Multiplier #(.mode("twosComplement"), .width(32)) multiplier_1 (
    .a(X), .b(Y), .out(multiplier_1_out), .cout(multiplier_1_cout));  // open: cin
  Divider #(.mode("twosComplement"), .width(32)) divider_1 (
    .a(X), .b(Y), .out(divider_1_out), .rem(divider_1_rem));  // open: upper
  Bit_Extender #(.in_width(32), .out_width(5), .\type ("zero")) bit_extender_1 (.in(Y), .out(bit_extender_1_out));
  Negator #(.width(32)) negator_1 (.in(X), .out(negator_1_out));
  Shifter #(.width(32)) shifter_1 (.in(X), .\dist (bit_extender_1_out), .out(shifter_1_out));
  Shifter #(.shift("lr"), .width(32)) shifter_2 (.in(X), .\dist (bit_extender_1_out), .out(shifter_2_out));
  Multiplexer #(.select(3), .width(32)) multiplexer_1 (
    .in0(X), .in1(adder_1_out), .in2(subtractor_1_out), .in3(multiplier_1_out), .in4(divider_1_out),
    .in5(negator_1_out), .in6(shifter_1_out), .in7(shifter_2_out), .out({flags[0], Xout[30:0]}),
    .sel({op2, op1, op0}));
  Comparator #(.width(32)) comparator_1 (.a(X), .b(Y), .eq(flags[1]));  // open: gt, lt
  Multiplexer #(.select(3), .width(32)) multiplexer_2 (
    .in0({32{1'b0}}), .in1({32{1'b0}}), .in2({32{1'b0}}), .in3(undriven), .in4(multiplier_1_cout),
    .in5(divider_1_rem), .in6({32{1'b0}}), .in7({32{1'b0}}), .out(Yout), .sel({op2, op1, op0}));
  Multiplexer #(.select(3)) multiplexer_3 (
    .in0(1'b0), .in1(adder_1_cout), .in2(1'b0), .in3(1'b0), .in4(1'b0), .in5(1'b0), .in6(1'b0), .in7(1'b0),
    .out(flags[2]), .sel({op2, op1, op0}));

  assign flags[3] = ic;
  assign Xout[31] = flags[0];
endmodule

module logical_unit (
  input  ic,
  input  cf,
  input  op2,
  input  op1,
  input  op0,
  input  [31:0] X,
  input  [31:0] Y,
  output [3:0] flags,
  output [31:0] Xout,
  output [31:0] Yout
);

  wire [31:0] and_1_out, nand_1_out, nor_1_out, not_1_out, or_1_out, xnor_1_out, xor_1_out;

  assign and_1_out = X & Y;  // AND_Gate and_1, 32 bits wide
  assign or_1_out = X | Y;  // OR_Gate or_1, 32 bits wide
  assign nand_1_out = ~(X & Y);  // NAND_Gate nand_1, 32 bits wide
  assign nor_1_out = ~(X | Y);  // NOR_Gate nor_1, 32 bits wide
  assign not_1_out = ~X;  // NOT_Gate not_1, 32 bits wide
  assign xor_1_out = X ^ Y;  // XOR_Gate xor_1, 32 bits wide
  Multiplexer #(.select(3), .width(32)) multiplexer_1 (
    .in0(X), .in1(and_1_out), .in2(or_1_out), .in3(nand_1_out), .in4(nor_1_out), .in5(not_1_out),
    .in6(xor_1_out), .in7(xnor_1_out), .out(Xout), .sel({op2, op1, op0}));
  assign xnor_1_out = ~(X ^ Y);  // XNOR_Gate xnor_1, 32 bits wide
  Comparator #(.width(32)) comparator_1 (.a(Xout), .b({32{1'b0}}), .eq(flags[1]), .lt(flags[0]));  // open: gt

  assign flags[3:2] = {ic, cf};
  assign Yout = {32{1'b0}};
endmodule

module ALU_instruction (
  input  [3:0] flags,
  input  [31:0] instruction,
  input  [31:0] r0,
  input  [31:0] r1,
  input  [31:0] r2,
  input  [31:0] r3,
  input  [31:0] r4,
  input  [31:0] r5,
  input  [31:0] r6,
  input  [31:0] r7,
  input  [31:0] sp,
  input  [31:0] bp,
  input  [31:0] ip,
  input  [31:0] ar,
  input  [31:0] ar_ptr,
  input  [31:0] io,
  input  [31:0] X,
  output [3:0] flags_out,
  output [31:0] Xout,
  output [31:0] Yout,
  output sr0,
  output sr1,
  output sr2,
  output sr3,
  output sr4,
  output sr5,
  output sr6,
  output sr7,
  output ssp,
  output sbp,
  output sip,
  output sar,
  output sar_ptr,
  output sio
);

  wire not_1_out;
  wire [31:0] multiplexer_1_out, multiplexer_2_out;

  Multiplexer #(.select(4), .width(32)) multiplexer_1 (
    .in0(r0), .in1(r1), .in2(r2), .in3(r3), .in4(r4), .in5(r5), .in6(r6), .in7(r7), .in8(sp), .in9(bp),
    .in10(ip), .in11(ar), .in12(ar_ptr), .in13(io), .in14(X), .out(multiplexer_1_out), .sel(instruction[12:9]));  // open: in15
  Multiplexer #(.select(4), .width(32)) multiplexer_2 (
    .in0(r0), .in1(r1), .in2(r2), .in3(r3), .in4(r4), .in5(r5), .in6(r6), .in7(r7), .in8(sp), .in9(bp),
    .in10(ip), .in11(ar), .in12(ar_ptr), .in13(io), .in14(X), .out(multiplexer_2_out), .sel(instruction[8:5]));  // open: in15
  ALU alu_1 (
    .cf(flags[2]), .ic(flags[3]), .op3(instruction[3]), .op2(instruction[2]), .op1(instruction[1]),
    .op0(instruction[0]), .X(multiplexer_1_out), .Y(multiplexer_2_out), .flags(flags_out), .Xout(Xout),
    .Yout(Yout));
  not not_1 (not_1_out, instruction[4]);
  Demultiplexer #(.select(4)) demultiplexer_1 (
    .out0(sr0), .out1(sr1), .out2(sr2), .out3(sr3), .out4(sr4), .out5(sr5), .out6(sr6), .out7(sr7),
    .out8(ssp), .out9(sbp), .out10(sip), .out11(sar), .out12(sar_ptr), .out13(sio), .in(not_1_out),
    .sel(instruction[8:5]));  // open: out14, out15
endmodule

module non_ALU_instruction (
  input  [3:0] flags,
  input  [31:0] instruction,
  input  [31:0] r0,
  input  [31:0] r1,
  input  [31:0] r2,
  input  [31:0] r3,
  input  [31:0] r4,
  input  [31:0] r5,
  input  [31:0] r6,
  input  [31:0] r7,
  input  [31:0] sp,
  input  [31:0] bp,
  input  [31:0] ip,
  input  [31:0] ar,
  input  [31:0] ar_ptr,
  input  [31:0] io,
  input  [31:0] X,
  output [3:0] flags_out,
  output [31:0] Xout,
  output [31:0] Yout,
  output sr0,
  output sr1,
  output sr2,
  output sr3,
  output sr4,
  output sr5,
  output sr6,
  output sr7,
  output ssp,
  output sbp,
  output sip,
  output sar,
  output sar_ptr,
  output sio
);

  wire and_2_out, nor_1_out, or_1_out;
  wire [3:0] and_1_out;

  nor nor_1 (nor_1_out, instruction[0], instruction[1], instruction[2], instruction[3]);
  assign and_1_out = instruction[16:13] & flags;  // AND_Gate and_1, 4 bits wide
  Multiplexer #(.select(4), .width(32)) multiplexer_1 (
    .in0(r0), .in1(r1), .in2(r2), .in3(r3), .in4(r4), .in5(r5), .in6(r6), .in7(r7), .in8(sp), .in9(bp),
    .in10(ip), .in11(ar), .in12(ar_ptr), .in13(io), .in14(X), .sel(instruction[12:9]));  // open: in15, out
  Multiplexer #(.select(4), .width(32)) multiplexer_2 (
    .in0(r0), .in1(r1), .in2(r2), .in3(r3), .in4(r4), .in5(r5), .in6(r6), .in7(r7), .in8(sp), .in9(bp),
    .in10(ip), .in11(ar), .in12(ar_ptr), .in13(io), .in14(X), .sel(instruction[8:5]));  // open: in15, out
  and and_2 (and_2_out, nor_1_out, instruction[4]);
  or or_1 (or_1_out, and_1_out[0], and_1_out[1], and_1_out[2], and_1_out[3]);
  // AND_Gate and_3 has open pins: in0=or_1_out, out=open
  Demultiplexer #(.select(4)) demultiplexer_1 (
    .out0(sr0), .out1(sr1), .out2(sr2), .out3(sr3), .out4(sr4), .out5(sr5), .out6(sr6), .out7(sr7),
    .out8(ssp), .out9(sbp), .out10(sip), .out11(sar), .out12(sar_ptr), .out13(sio), .in(and_2_out),
    .sel(instruction[8:5]));  // open: out14, out15
endmodule
